# Fritzing sketch wiring eletric (saved by Fritzing 0.9.3b)

parts:
  U1 = ESP32-38PinWide [part_number=ESP32-38PinWide]
  J2 = Power Jack [package=power_jack_smd]
  S5 = SPST Switch [package=switch-spdt-smd]
  J9 = female pin header, 1 pin [form="♀ (female)"]
  J10 = female pin header, 1 pin [form="♀ (female)"]
  M1 = Pzem-004t
  DS1 = DS18B20 1-Wire Temperature Sensor Probe
  KB1 = 1*4 Membrane Matrix Keypad
  A1 = Current transformer PZCT02
  Part1 = Lilypad Battery Connect
  J18 = female pin header, 1 pin [form="♀ (female)"]
  J19 = female pin header, 1 pin [form="♀ (female)"]
  J20 = female pin header, 1 pin [form="♀ (female)"]
  J21 = female pin header, 1 pin [form="♀ (female)"]
  R5 = Resistor [tolerance=±5% resistance=220 package="2010 [SMD]"]  # not connected
  R6 = Resistor [tolerance=±5% resistance=220 package="2010 [SMD]"]
  J22 = female pin header, 1 pin [form="♀ (female)"]
  J23 = female pin header, 1 pin [form="♀ (female)"]
  R8 = Resistor [tolerance=±5% resistance=220 package="2010 [SMD]"]  # not connected
  R9 = Resistor [tolerance=±5% resistance=220 package="2010 [SMD]"]
  R10 = Resistor [tolerance=±5% resistance=220 package="2010 [SMD]"]
  R11 = Resistor [tolerance=±5% resistance=220 package="2010 [SMD]"]
  J24 = female pin header, 1 pin [form="♀ (female)"]  # not connected
  J25 = female pin header, 1 pin [form="♀ (female)"]  # not connected
  J26 = female pin header, 1 pin [form="♀ (female)"]
  J27 = female pin header, 1 pin [form="♀ (female)"]

nets:
  N1: U1.3.3, J10.pin1, DS1.VDD, R6.Pin_1, J22.pin1
  N2: U1.GPIO33, KB1.pin5, R11.Pin_0, J27.pin1
  N3: U1.GPIO26, KB1.pin4, R10.Pin_0, J26.pin1
  N4: U1.GPIO27, KB1.pin3, R9.Pin_0
  N5: U1.GPIO14, KB1.pin2
  GND: U1.GND, M1.GND, DS1.GND
  N6: U1.GPIO11, J2.GNDBREAK, J9.pin1, KB1.pin1
  VIN: U1.VIN, S5.O, M1.5V
  N7: U1.GPIO4, DS1.DQ, R6.Pin_0, J23.pin1
  N8: U1.GPIO3, M1.TX
  N9: U1.GPIO1, M1.RX
  N10: J2.GND, S5.P
  N11: M1.LOUT, Part1.-
  N12: M1.LIN, Part1.+, J18.pin1, J20.pin1
  N13: M1.NIN, A1.Pin_1
  N14: M1.NOUT, A1.Pin_2
  N15: J19.pin1, J21.pin1

notes:
  INPUT POWER
  ON/OFF
  DS18b20
  SENSOR PZEM
  220 AC
  UP
  RESET
  SET
  DOWN

custom parts:
  ESP32-38PinWide: Generic 38-Pin ESP32 with wide format (only access to one side of pins on a breadboard) based on Stephen Lilley's HiLetgo ESP-WROOM-32 ESP32 ESP-32S Development Board.
  Pzem-004t: Pzem-004t used for measuring AC voltage, current, active power, frequency, power factor and active energy, the module is without display function, the data is read through the TTL interface.
  1*4 Membrane Matrix Keypad: Membrane Matrix 1x4 Keypad
  Current transformer PZCT02: Current transformer PZCT02.
